// Digital circuit Lab02.dig as structural Verilog
module Lab02 (
  input  B,
  input  C,
  input  A,
  input  D,
  output Fa,
  output Fb,
  output Fc,
  output Fd,
  output Fe,
  output Fg,
  output Ff
);

  wire and_1_out, and_2_out, and_3_out, and_4_out, and_5_out, and_6_out, and_7_out, and_8_out, and_9_out,
       and_10_out, and_11_out, and_12_out, and_13_out, and_14_out, and_15_out, and_16_out, and_17_out,
       and_18_out, and_19_out, and_20_out, and_21_out, and_22_out, and_23_out, and_24_out, and_25_out,
       and_26_out, and_27_out, and_28_out, and_29_out, and_30_out, and_31_out, and_32_out, nA, nB, nC, nD;

  not not_1 (nA, A);
  not not_2 (nB, B);
  not not_3 (nC, C);
  not not_4 (nD, D);
  and and_1 (and_1_out, A, nC, nB);
  and and_2 (and_2_out, D, nA, B);
  and and_3 (and_3_out, B, C);
  and and_4 (and_4_out, nA, C);
  and and_5 (and_5_out, nB, nD);
  and and_6 (and_6_out, A, nC, D);
  and and_7 (and_7_out, nD, nC, nA);
  and and_8 (and_8_out, nA, D, C);
  and and_9 (and_9_out, nA, nB);
  and and_10 (and_10_out, nB, nD);
  and and_11 (and_11_out, nA, nC);
  and and_12 (and_12_out, nA, D);
  and and_13 (and_13_out, nC, D);
  and and_14 (and_14_out, nA, B);
  and and_15 (and_15_out, A, nB);
  and and_16 (and_16_out, B, nC, D);
  and and_17 (and_17_out, nD, B, C);
  and and_18 (and_18_out, nB, C, D);
  and and_19 (and_19_out, A, nC);
  and and_20 (and_20_out, nA, nB, nD);
  and and_21 (and_21_out, C, nD);
  and and_22 (and_22_out, A, B);
  and and_23 (and_23_out, A, C);
  and and_24 (and_24_out, nB, nD);
  and and_25 (and_25_out, nA, nC, nD);
  and and_26 (and_26_out, B, nC, nA);
  and and_27 (and_27_out, B, nD, C);
  and and_28 (and_28_out, A, nB);
  and and_29 (and_29_out, C, A);
  and and_30 (and_30_out, B, nC);
  and and_31 (and_31_out, C, nD);
  and and_32 (and_32_out, nB, C);
  or or_1 (Fa, and_1_out, and_2_out, and_3_out, and_4_out, and_5_out);
  or or_2 (Fb, and_6_out, and_7_out, and_8_out, and_9_out, and_10_out);
  or or_3 (Fc, and_11_out, and_12_out, and_13_out, and_14_out, and_15_out);
  or or_4 (Fd, and_16_out, and_17_out, and_18_out, and_19_out, and_20_out);
  or or_5 (Fe, and_21_out, and_22_out, and_23_out, and_24_out);
  or or_6 (Ff, and_25_out, and_26_out, and_27_out, and_28_out, and_29_out);
  or or_7 (Fg, A, and_30_out, and_31_out, and_32_out);

  // Other names for the same wires on the sheet: Faa = Fa; Fbb = Fb; Fcc = Fc; Fdd = Fd; Fee = Fe; Fff = Ff; Fgg = Fg
endmodule
