// Digital circuit control-unit.dig as structural Verilog
module control_unit (
  input  [6:0] opcode,
  input  [2:0] funct3,
  input  [6:0] funct7,
  output [3:0] ALUOp,
  output [1:0] ImmSrc,
  output ALUSrc,
  output RegWrite
);

  wire add, addi, \and , andi, funct3_000, funct3_010, funct3_110, funct3_111, funct7_0x00, funct7_0x20,
       opcode_i, opcode_r, \or , priorityencoder_1_any, slt, slti, sub;
  wire [2:0] priorityencoder_1_num;

  Comparator #(.Bits(7)) comparator_1 (.a(opcode), .b(7'b0110011), .eq(opcode_r));  // open: gt, lt
  Comparator #(.Bits(7)) comparator_2 (.a(opcode), .b(7'b0010011), .eq(opcode_i));  // open: gt, lt
  Comparator #(.Bits(7)) comparator_3 (.a(funct7), .b({7{1'b0}}), .eq(funct7_0x00));  // open: gt, lt
  Comparator #(.Bits(7)) comparator_4 (.a(funct7), .b(7'b0100000), .eq(funct7_0x20));  // open: gt, lt
  Decoder #(.Selector_Bits(3)) decoder_1 (
    .sel(funct3), .out_0(funct3_000), .out_2(funct3_010), .out_6(funct3_110), .out_7(funct3_111));  // open: out_1, out_3, out_4, out_5
  and and_1 (add, opcode_r, funct7_0x00, funct3_000);
  and and_2 (\and , opcode_r, funct7_0x00, funct3_111);
  and and_3 (addi, opcode_i, funct3_000);
  PriorityEncoder #(.Selector_Bits(3)) priorityencoder_1 (
    .in0(add), .in1(sub), .in2(\and ), .in3(\or ), .in4(slt), .in5(addi), .in6(slti), .in7(andi),
    .num(priorityencoder_1_num), .any(priorityencoder_1_any));
  and and_4 (slt, opcode_r, funct7_0x00, funct3_010);
  and and_5 (andi, opcode_i, funct3_111);
  ROM #(.AddrBits(3), .Bits(8)) rom_1 (
    .A(priorityencoder_1_num), .sel(priorityencoder_1_any), .D({RegWrite, ALUSrc, ImmSrc, ALUOp}));
  and and_6 (sub, opcode_r, funct7_0x20, funct3_000);
  and and_7 (\or , opcode_r, funct7_0x00, funct3_110);
  and and_8 (slti, opcode_i, funct3_010);

  // Notes on the sheet:
  //   Conditions
  //   R-type
  //   I-type
  //   Translator
  //   contents of rom_1 (hex, n*v repeats v):
  //   82,86,80,81,87,c2,c7,c0
endmodule

/* Test case control-unit:
opcode   funct3  funct7    RegWrite ALUSrc ImmSrc ALUOp
0b0110011 0b000  0b0000000 0b1      0b0    0b00   0b0010
0b0110011 0b000  0b0100000 0b1      0b0    0b00   0b0110
0b0110011 0b111  0b0000000 0b1      0b0    0b00   0b0000
0b0110011 0b110  0b0000000 0b1      0b0    0b00   0b0001
0b0110011 0b010  0b0000000 0b1      0b0    0b00   0b0111
0b0010011 0b000  0b0000000 0b1      0b1    0b00   0b0010
0b0010011 0b010  0b0000000 0b1      0b1    0b00   0b0111
0b0010011 0b111  0b0000000 0b1      0b1    0b00   0b0000
*/
