// Digital circuit register-file.dig as structural Verilog
module register_file (
  input  [4:0] ReadReg1,
  input  [4:0] ReadReg2,
  input  [4:0] WriteReg,
  input  [31:0] WriteData,
  input  RegWrite,
  input  Clock,
  output [31:0] ReadData1,
  output [31:0] ReadData2
);

  wire En_1, En_2, En_3, En_4, En_5, En_6, En_7, En_8, En_9, En_10, En_11, En_12, En_13, En_14, En_15, En_16,
       En_17, En_18, En_19, En_20, En_21, En_22, En_23, En_24, En_25, En_26, En_27, En_28, En_29, En_30,
       En_31;
  wire [4:0] and_1_out, bitextender_1_out;
  wire [31:0] Reg_0, Reg_1, Reg_2, Reg_3, Reg_4, Reg_5, Reg_6, Reg_7, Reg_8, Reg_9, Reg_10, Reg_11, Reg_12,
       Reg_13, Reg_14, Reg_15, Reg_16, Reg_17, Reg_18, Reg_19, Reg_20, Reg_21, Reg_22, Reg_23, Reg_24,
       Reg_25, Reg_26, Reg_27, Reg_28, Reg_29, Reg_30, Reg_31;

  Multiplexer #(.Selector_Bits(5), .Bits(32)) multiplexer_1 (
    .sel(ReadReg1), .in_0(Reg_0), .in_1(Reg_1), .in_2(Reg_2), .in_3(Reg_3), .in_4(Reg_4), .in_5(Reg_5),
    .in_6(Reg_6), .in_7(Reg_7), .in_8(Reg_8), .in_9(Reg_9), .in_10(Reg_10), .in_11(Reg_11), .in_12(Reg_12),
    .in_13(Reg_13), .in_14(Reg_14), .in_15(Reg_15), .in_16(Reg_16), .in_17(Reg_17), .in_18(Reg_18),
    .in_19(Reg_19), .in_20(Reg_20), .in_21(Reg_21), .in_22(Reg_22), .in_23(Reg_23), .in_24(Reg_24),
    .in_25(Reg_25), .in_26(Reg_26), .in_27(Reg_27), .in_28(Reg_28), .in_29(Reg_29), .in_30(Reg_30),
    .in_31(Reg_31), .out(ReadData1));
  Multiplexer #(.Selector_Bits(5), .Bits(32)) multiplexer_2 (
    .sel(ReadReg2), .in_0(Reg_0), .in_1(Reg_1), .in_2(Reg_2), .in_3(Reg_3), .in_4(Reg_4), .in_5(Reg_5),
    .in_6(Reg_6), .in_7(Reg_7), .in_8(Reg_8), .in_9(Reg_9), .in_10(Reg_10), .in_11(Reg_11), .in_12(Reg_12),
    .in_13(Reg_13), .in_14(Reg_14), .in_15(Reg_15), .in_16(Reg_16), .in_17(Reg_17), .in_18(Reg_18),
    .in_19(Reg_19), .in_20(Reg_20), .in_21(Reg_21), .in_22(Reg_22), .in_23(Reg_23), .in_24(Reg_24),
    .in_25(Reg_25), .in_26(Reg_26), .in_27(Reg_27), .in_28(Reg_28), .in_29(Reg_29), .in_30(Reg_30),
    .in_31(Reg_31), .out(ReadData2));
  Decoder #(.Selector_Bits(5)) decoder_1 (
    .sel(and_1_out), .out_1(En_1), .out_2(En_2), .out_3(En_3), .out_4(En_4), .out_5(En_5), .out_6(En_6),
    .out_7(En_7), .out_8(En_8), .out_9(En_9), .out_10(En_10), .out_11(En_11), .out_12(En_12), .out_13(En_13),
    .out_14(En_14), .out_15(En_15), .out_16(En_16), .out_17(En_17), .out_18(En_18), .out_19(En_19),
    .out_20(En_20), .out_21(En_21), .out_22(En_22), .out_23(En_23), .out_24(En_24), .out_25(En_25),
    .out_26(En_26), .out_27(En_27), .out_28(En_28), .out_29(En_29), .out_30(En_30), .out_31(En_31));  // open: out_0
  assign and_1_out = WriteReg & bitextender_1_out;  // And and_1, 5 bits wide
  BitExtender #(.inputBits(1), .outputBits(5)) bitextender_1 (.in(RegWrite), .out(bitextender_1_out));
  Register #(.Bits(32)) u_Reg_0 (.D({32{1'b0}}), .C(Clock), .en(1'b0), .Q(Reg_0));
  Register #(.Bits(32)) u_Reg_4 (.D(WriteData), .C(Clock), .en(En_4), .Q(Reg_4));
  Register #(.Bits(32)) u_Reg_8 (.D(WriteData), .C(Clock), .en(En_8), .Q(Reg_8));
  Register #(.Bits(32)) u_Reg_12 (.D(WriteData), .C(Clock), .en(En_12), .Q(Reg_12));
  Register #(.Bits(32)) u_Reg_16 (.D(WriteData), .C(Clock), .en(En_16), .Q(Reg_16));
  Register #(.Bits(32)) u_Reg_20 (.D(WriteData), .C(Clock), .en(En_20), .Q(Reg_20));
  Register #(.Bits(32)) u_Reg_24 (.D(WriteData), .C(Clock), .en(En_24), .Q(Reg_24));
  Register #(.Bits(32)) u_Reg_28 (.D(WriteData), .C(Clock), .en(En_28), .Q(Reg_28));
  Register #(.Bits(32)) u_Reg_1 (.D(WriteData), .C(Clock), .en(En_1), .Q(Reg_1));
  Register #(.Bits(32)) u_Reg_5 (.D(WriteData), .C(Clock), .en(En_5), .Q(Reg_5));
  Register #(.Bits(32)) u_Reg_9 (.D(WriteData), .C(Clock), .en(En_9), .Q(Reg_9));
  Register #(.Bits(32)) u_Reg_13 (.D(WriteData), .C(Clock), .en(En_13), .Q(Reg_13));
  Register #(.Bits(32)) u_Reg_17 (.D(WriteData), .C(Clock), .en(En_17), .Q(Reg_17));
  Register #(.Bits(32)) u_Reg_21 (.D(WriteData), .C(Clock), .en(En_21), .Q(Reg_21));
  Register #(.Bits(32)) u_Reg_25 (.D(WriteData), .C(Clock), .en(En_25), .Q(Reg_25));
  Register #(.Bits(32)) u_Reg_29 (.D(WriteData), .C(Clock), .en(En_29), .Q(Reg_29));
  Register #(.Bits(32)) u_Reg_2 (.D(WriteData), .C(Clock), .en(En_2), .Q(Reg_2));
  Register #(.Bits(32)) u_Reg_6 (.D(WriteData), .C(Clock), .en(En_6), .Q(Reg_6));
  Register #(.Bits(32)) u_Reg_10 (.D(WriteData), .C(Clock), .en(En_10), .Q(Reg_10));
  Register #(.Bits(32)) u_Reg_14 (.D(WriteData), .C(Clock), .en(En_14), .Q(Reg_14));
  Register #(.Bits(32)) u_Reg_18 (.D(WriteData), .C(Clock), .en(En_18), .Q(Reg_18));
  Register #(.Bits(32)) u_Reg_22 (.D(WriteData), .C(Clock), .en(En_22), .Q(Reg_22));
  Register #(.Bits(32)) u_Reg_26 (.D(WriteData), .C(Clock), .en(En_26), .Q(Reg_26));
  Register #(.Bits(32)) u_Reg_30 (.D(WriteData), .C(Clock), .en(En_30), .Q(Reg_30));
  Register #(.Bits(32)) u_Reg_3 (.D(WriteData), .C(Clock), .en(En_3), .Q(Reg_3));
  Register #(.Bits(32)) u_Reg_7 (.D(WriteData), .C(Clock), .en(En_7), .Q(Reg_7));
  Register #(.Bits(32)) u_Reg_11 (.D(WriteData), .C(Clock), .en(En_11), .Q(Reg_11));
  Register #(.Bits(32)) u_Reg_15 (.D(WriteData), .C(Clock), .en(En_15), .Q(Reg_15));
  Register #(.Bits(32)) u_Reg_19 (.D(WriteData), .C(Clock), .en(En_19), .Q(Reg_19));
  Register #(.Bits(32)) u_Reg_23 (.D(WriteData), .C(Clock), .en(En_23), .Q(Reg_23));
  Register #(.Bits(32)) u_Reg_27 (.D(WriteData), .C(Clock), .en(En_27), .Q(Reg_27));
  Register #(.Bits(32)) u_Reg_31 (.D(WriteData), .C(Clock), .en(En_31), .Q(Reg_31));

  // Other names for the same wires on the sheet: Clk = Clock
endmodule

/* Test case Register File Test:
WriteReg WriteData RegWrite Clock ReadReg1 ReadReg2 ReadData1 ReadData2

# $1 = 25
1 25 1 C 1 0 25 0

# $2 = 30
2 30 1 C 0 2 0 30

# $(N+1) = (N+1)
loop(N, 30)
	(N+1) (N+1) 1 C (N+1) (N) (N+1) (N)
end loop

# $(N+1) = N-60
loop(N, 30)
	(N+1) (N-60) 1 C (N+1) (N+1) (N-60) (N-60)
end loop

# Try writing to $0. This should not write anything
0 25 1 C 0 0 0 0

# try writing when RegWrite = 0
# (the registers should still have their old values)
loop(N, 30)
	(N+1) (N+80) 0 C (N+1) (N+1) (N-60) (N-60)
end loop
*/
